# Fritzing sketch sheme (saved by Fritzing 0.9.3b)
breadboards: 1

parts:
  U1 = ESP8266 WiFi Module [part_number=ESP8266]
  U2 = SWITCH_SPDT [package=kps-1290]
  Power_plug1 = Power plug
  Power_plug2 = Power plug
  BB2 = 4-Line Bi-Directional Level Shifter
  DS1 = DS18B20 1-Wire Temperature Sensor [part_number=DS18B20]
  R1 = Resistor [tolerance=±5% resistance=2.2k package=THT]
  LED1 = LED - 5mm [color="Red (633nm)" package="5 mm [THT]"]
  R2 = Resistor [tolerance=±5% resistance=1M package=THT]
  KY-4 = Keyes Relay [package=THT]
  Power_plug3 = Power plug
  Power_plug4 = Power plug

nets:
  VCC: U1.VCC, U1.CH_PD, U2.O, Power_plug1.VCC, BB2.LV, DS1.VDD, R1.Pin_0
  GND: U1.GND, Power_plug1.GND, BB2.GND#6, DS1.GND, LED1.cathode, R2.Pin_1
  N1: U1.GPIO_4, BB2.A4
  N2: U1.GPIO_5, LED1.anode
  N3: U1.GPIO_14, U2.P
  N4: U1.GPIO_13, DS1.DQ, R1.Pin_1
  N5: U2.S, R2.Pin_0
  N6: Power_plug2.GND, BB2.GND#16, KY-4.ground
  N7: Power_plug2.VCC, BB2.HV, KY-4.power
  N8: BB2.B4, KY-4.signal
  N9: KY-4.C, Power_plug3.VCC
  N10: KY-4.NO, Power_plug4.VCC
  GND_2: Power_plug3.GND, Power_plug4.GND

notes:
  3.3V
  5V
  250V AC
  Boiler oower supply

custom parts:
  ESP8266 WiFi Module: Generic WiFi Module based on the ESP8266 with onboard PCB antenna and UART communications
  4-Line Bi-Directional Level Shifter: 4-Channel Bi-Directional Level Shifter
  Keyes Relay: The Keyes 5V relay module is suitable for SCM development, home appliance control. It uses a 5V~12V TIL control signal which can control DC / AC signal.
